// Logisim project nand2tetris.circ as structural Verilog: 5 circuits, main circuit main
module main (
  input  [15:0] in_1,
  input  in_2,
  input  in_3,
  input  in_4,
  input  in_5,
  input  [15:0] in_6,
  input  in_7,
  input  in_8,
  input  [15:0] in_9,
  input  in_10,
  input  in_11,
  input  in_12,
  output [15:0] out_13,
  output [15:0] out_14
);

  wire clock_1_out;

  // ALU_16bit alu_16bit_1: pin names not known; wires that end beside it: in_1, in_2, in_3, in_4, in_5, in_6, in_7, in_8, out_13
  Clock clock_1 (.out(clock_1_out));
  PC_16bit pc_16bit_1 (
    .Input1(in_9), .Load(in_10), .Reset(in_11), .Increment(in_12), .Clock(clock_1_out), .out_6(out_14));
endmodule

module ALU_16bit (
  input  [15:0] InputX,
  input  ZX,
  input  NX,
  input  [15:0] InputY,
  input  ZY,
  input  NY,
  input  F,
  input  N0,
  output [15:0] Output1
);

  wire [15:0] adder_1_out, and_1_out, multiplexer_1_out, multiplexer_2_out, multiplexer_3_out,
       multiplexer_4_out, multiplexer_5_out, not_1_out, not_2_out, not_3_out;

  Multiplexer #(.width(16)) multiplexer_1 (.in0(InputX), .in1({16{1'b0}}), .out(multiplexer_1_out), .sel(ZX));
  Multiplexer #(.width(16)) multiplexer_2 (.in0(InputY), .in1({16{1'b0}}), .out(multiplexer_2_out), .sel(ZY));
  assign not_1_out = ~multiplexer_1_out;  // NOT_Gate not_1, 16 bits wide
  Multiplexer #(.width(16)) multiplexer_3 (.in0(multiplexer_2_out), .in1(not_2_out), .out(multiplexer_3_out), .sel(NY));
  assign not_2_out = ~multiplexer_2_out;  // NOT_Gate not_2, 16 bits wide
  Multiplexer #(.width(16)) multiplexer_4 (.in0(multiplexer_1_out), .in1(not_1_out), .out(multiplexer_4_out), .sel(NX));
  assign and_1_out = multiplexer_4_out & multiplexer_3_out;  // AND_Gate and_1, 16 bits wide
  Adder #(.width(16)) adder_1 (.a(multiplexer_4_out), .b(multiplexer_3_out), .out(adder_1_out));  // open: cin, cout
  Multiplexer #(.width(16)) multiplexer_5 (.in0(and_1_out), .in1(adder_1_out), .out(multiplexer_5_out), .sel(F));
  assign not_3_out = ~multiplexer_5_out;  // NOT_Gate not_3, 16 bits wide
  Multiplexer #(.width(16)) multiplexer_6 (.in0(multiplexer_5_out), .in1(not_3_out), .out(Output1), .sel(N0));
endmodule

module PC_16bit (
  input  [15:0] Input1,
  input  Load,
  input  Reset,
  input  Increment,
  input  Clock,
  output [15:0] out_6
);

  wire and_1_out, not_1_out, or_1_out;
  wire [15:0] adder_1_out, multiplexer_1_out, multiplexer_2_out, multiplexer_3_out;

  Multiplexer #(.width(16)) multiplexer_1 (.in0({16{1'b0}}), .in1(Input1), .out(multiplexer_1_out), .sel(Load));
  Adder #(.width(16)) adder_1 (.a(out_6), .b(16'h1), .out(adder_1_out));  // open: cin, cout
  Multiplexer #(.width(16)) multiplexer_2 (
    .in0(multiplexer_1_out), .in1(adder_1_out), .out(multiplexer_2_out), .sel(and_1_out));
  and and_1 (and_1_out, Increment, not_1_out);
  not not_1 (not_1_out, Load);
  Multiplexer #(.width(16)) multiplexer_3 (
    .in0(multiplexer_2_out), .in1({16{1'b0}}), .out(multiplexer_3_out), .sel(Reset));
  or or_1 (or_1_out, Load, Increment, Reset);
  Register #(.width(16)) register_1 (.D(multiplexer_3_out), .en(or_1_out), .clk(Clock), .Q(out_6));  // open: clr

  // Other names for the same wires on the sheet: Register_Output[15:0] = out_6
endmodule

module CPU_16bit (
  input  [15:0] InM,
  input  [15:0] Instruction,
  input  Reset,
  input  Clock,
  output [15:0] OutMAddress,
  output [15:0] OutM,
  output M_WE
);

  Register Reg_A ();  // open: D, en, clk, Q, clr
  Register Reg_D ();  // open: D, en, clk, Q, clr
  ALU_16bit alu_16bit_1 ();  // open: InputX, ZX, NX, InputY, ZY, NY, F, N0, Output1
  PC_16bit pc_16bit_1 ();  // open: Input1, Load, Reset, Increment, Clock, out_6
endmodule

module ControlLogic_16bit (
  input  [15:0] Instruction,
  input  [15:0] InM,
  input  [15:0] A_Output,
  input  [15:0] D_Output,
  input  [15:0] ALUOutput,
  output [15:0] A_Data,
  output A_WE,
  output [15:0] D_Data,
  output D_WE,
  output [15:0] ALU_InputX,
  output [15:0] ALU_InputY,
  output [15:0] OutMAddress,
  output [15:0] OutM,
  output M_WE,
  output [15:0] PC_Input,
  output PC_Load,
  output PC_Increment
);

  wire and_1_out, and_2_out, and_3_out, and_4_out, comparator_1_eq, comparator_1_gt, comparator_1_lt,
       not_1_out;

  Comparator #(.width(16)) comparator_1 (
    .a(ALUOutput), .b({16{1'b0}}), .gt(comparator_1_gt), .eq(comparator_1_eq), .lt(comparator_1_lt));
  and and_1 (and_1_out, Instruction[15], comparator_1_gt);
  and and_2 (and_2_out, comparator_1_eq, Instruction[14]);
  and and_3 (and_3_out, comparator_1_lt, Instruction[13]);
  not not_1 (not_1_out, Instruction[0]);
  and and_4 (and_4_out, Instruction[0], Instruction[10]);
  or or_1 (PC_Load, and_1_out, and_2_out, and_3_out);
  Multiplexer #(.width(16)) multiplexer_1 (.in0(Instruction), .in1(ALUOutput), .out(A_Data), .sel(Instruction[0]));
  and and_5 (D_WE, Instruction[11], Instruction[0]);
  Multiplexer #(.width(16)) multiplexer_2 (.in0(A_Output), .in1(InM), .out(ALU_InputY), .sel(Instruction[3]));
  not not_2 (PC_Increment, PC_Load);
  or or_2 (A_WE, not_1_out, and_4_out);
  and and_6 (M_WE, Instruction[0], Instruction[12]);

  assign ALU_InputX = D_Output;
  assign D_Data = ALUOutput;
  assign OutM = ALUOutput;
  assign OutMAddress = A_Output;
  assign PC_Input = A_Output;

  // Other names for the same wires on the sheet: IsCInstruction = Instruction[0]; A = Instruction[3];
  //   C1 = Instruction[4]; C2 = Instruction[5]; C3 = Instruction[6]; C4 = Instruction[7]; C5 = Instruction[8];
  //   C6 = Instruction[9]; D1 = Instruction[10]; D2 = Instruction[11]; D3 = Instruction[12]; J1 = Instruction[13];
  //   J2 = Instruction[14]; J3 = Instruction[15]
endmodule
